# Fritzing sketch Sysjourney (saved by Fritzing 0.9.3b)

parts:
  Raspberry_Pi_Zero1 = Raspberry Pi Zero
  U1 = LCD-16X2 [package=lcd-16x2_noholes]
  Matrix_keypad1 = KEYPAD 4x4
  Part1 = RFID-RC522-v2
  J1 = Piezo Speaker
  R1 = Resistor [tolerance=±5% resistance=1k package=THT]

nets:
  3V3: Raspberry_Pi_Zero1.3v3, Part1.3.3V
  N1: Raspberry_Pi_Zero1.GPIO4, J1.pin2
  GND: Raspberry_Pi_Zero1.GND, U1.VSS, U1.R_W, U1.K, Part1.GND, J1.pin1, R1.Pin_1
  N2: Raspberry_Pi_Zero1.GPIO17, Matrix_keypad1.row4
  N3: Raspberry_Pi_Zero1.GPIO27, Matrix_keypad1.row3
  N4: Raspberry_Pi_Zero1.GPIO22, Matrix_keypad1.row2
  N5: Raspberry_Pi_Zero1.GPIO10, Part1.MOSI
  N6: Raspberry_Pi_Zero1.GPIO9, Part1.MISO
  N7: Raspberry_Pi_Zero1.GPIO11, Part1.SCK
  N8: Raspberry_Pi_Zero1.GPIO5, Matrix_keypad1.row1
  N9: Raspberry_Pi_Zero1.GPIO6, Matrix_keypad1.col4
  N10: Raspberry_Pi_Zero1.GPIO13, Matrix_keypad1.col3
  N11: Raspberry_Pi_Zero1.GPIO19, Matrix_keypad1.col2
  N12: Raspberry_Pi_Zero1.GPIO26, Matrix_keypad1.col1
  N13: Raspberry_Pi_Zero1.GPIO21, U1.DB7
  N14: Raspberry_Pi_Zero1.GPIO20, U1.DB6
  N15: Raspberry_Pi_Zero1.GPIO16, U1.DB5
  N16: Raspberry_Pi_Zero1.GPIO12, U1.DB4
  N17: Raspberry_Pi_Zero1.GPIO8, Part1.SDA
  N18: Raspberry_Pi_Zero1.GPIO25, Part1.RST
  N19: Raspberry_Pi_Zero1.GPIO23, U1.E
  N20: Raspberry_Pi_Zero1.GPIO18, U1.RS
  5V: Raspberry_Pi_Zero1.5V, U1.VDD, U1.A

custom parts:
  KEYPAD 4x4: Matrix keypad 16 buttons, 4 rows x 4 columns
  RFID-RC522-v2: A simple China made RFID-RC522 Reader; do check the pin labels, as this is a MFRC522 based clone.
